# Fritzing sketch schematic (saved by Fritzing 0.8.7b)
breadboards: 2

parts:
  Mod1 = Raspberry Pi Pico
  Mod2 = Raspberry Pi 4B
  KY-1 = Keyes Relay [package=THT]
  J1 = Basic Servo
  PIR2 = KS0052 PIR sensor
  PIR3 = KS0052 PIR sensor
  F1 = Fan - Ventilador [package=THT]
  IC1 = KS0234 [chip_label=?]
  IC2 = KS0234 [chip_label=?]
  S1 = KY-026
  Mod3 = KY-012 Active Buzzer Module [package="Breakout board"]
  LED1 = LED - 5mm [color="Red (633nm)" package="5 mm [THT]"]
  S3 = Square Pushbutton
  Εξάρτημα1 = SRF05 Ultrasonic Rangefinder
  FC-1 = Sound Sensor
  S4 = Square Pushbutton
  Mod4 = KY-018 Photoresistor Module [package="Breakout board"]
  T1 = LM35 Temperature Sensor [package="TO92 [THT]"]
  J3 = Basic Servo
  J4 = 2.1mm Barrel Jack with Terminal Block
  R1 = Resistor [tolerance=±5% resistance=1k package=THT]
  R3 = Resistor [tolerance=±5% resistance=2.2k package=THT]
  R4 = Resistor [tolerance=±5% resistance=220 package=THT]

nets:
  N1: Mod1.pin_1, PIR2.S
  N2: Mod1.pin_2, PIR3.S
  N3: Mod1.pin_4, IC1.S
  N4: Mod1.pin_5, IC2.S
  N5: Mod1.pin_6, Mod4.-
  N6: Mod1.pin_7, J1.pulse
  N7: Mod1.pin_9, J3.pulse
  N8: Mod1.pin_10, Mod2.GPIO21
  N9: Mod1.pin_11, Mod2.GPIO20
  N10: Mod1.pin_12, Mod2.GPIO16
  N11: Mod1.pin_14, Εξάρτημα1.Trig
  N12: Mod1.pin_15, R1.Pin_0, R3.Pin_0
  N13: Mod1.pin_16, KY-1.signal
  GND: Mod1.pin_18, Mod1.pin_38, Mod1.pin_42, KY-1.ground, J1.gnd, PIR2.GND, PIR3.GND, F1.GND, IC1.GND, IC2.GND, S1.pin2, Εξάρτημα1.GND, FC-1.GND, Mod4.S, T1.GND, J3.gnd, J4.NEG, R3.Pin_1
  N14: Mod1.pin_31, FC-1.OUT
  N15: Mod1.pin_32, T1.+Vs
  N16: Mod1.pin_34, S1.pin4
  VCC: Mod1.pin_36, PIR2.VCC, PIR3.VCC, S1.pin3, FC-1.VCC, Mod4.Vin, T1.Vout
  N17: Mod1.pin_40, Εξάρτημα1.VCC
  N18: Mod2.3V3, Mod3.NC
  N19: Mod2.GND, Mod3.-, S3.leg1, S4.leg1, R4.Pin_0
  N20: Mod2.GPIO14, LED1.anode
  N21: Mod2.GPIO15, Mod3.S
  N22: Mod2.GPIO12, S3.leg0
  N23: Mod2.GPIO26, S4.leg0
  VCC_2: KY-1.power, KY-1.NO, J1.vcc, IC1.VCC, IC2.VCC, J3.vcc, J4.POS
  N24: KY-1.C, F1.5V
  N25: LED1.cathode, R4.Pin_1
  N26: Εξάρτημα1.Echo, R1.Pin_1

custom parts:
  Raspberry Pi Pico: Raspberry Pi Pico. Based around the RP2040 microcontroller the Pico is a low cost microcontroller device bringing Raspberry Pi quality, cost, and easy of use to the microcontroller space. Jan 2021, Split part in to two versions: tht (this one) and SMD. This one will drill holes for a .1 in header in pcb to allow plugging in the module as well as providing pads to solder the module to the top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
  Keyes Relay: The Keyes 5V relay module is suitable for SCM development, home appliance control. It uses a 5V~12V TIL control signal which can control DC / AC signal.
  KS0052 PIR sensor: PIR sensor
  Fan - Ventilador: Ventilador de 2 pines, se encuentra comunmente en computadoras de escritorio
  KS0234: Led yellow
  KY-026: ky-026 flame sensor module
  KY-012 Active Buzzer Module: Active Piezoelectric Buzzer Module KY-012, it produces single-tone sound when signal is high. (Special thanks to vanepp for fixing the PCB holes and other errors)
  KY-018 Photoresistor Module: KY-018 Photoresistor module, used to measure light intensity. It can determine the presence or absence of light.
